# Fritzing sketch schéma barre led (saved by Fritzing 0.9.3b)
circuit board: 8.31673cm x 4.10913cm
breadboards: 1

parts:
  R1 = Resistor [tolerance=±5% resistance=1k package=THT]
  Q1 = NPN-Transistor [package="TO92 [THT]"]
  Q2 = NPN-Transistor [package="TO92 [THT]"]
  Q3 = NPN-Transistor [package="TO92 [THT]"]
  Composant1 = Arduino Nano (Rev3.0)
  U1 = POT [package=pot_alpha_rv16af-20]
  R2 = Resistor [tolerance=±5% resistance=1k package=THT]
  R3 = Resistor [tolerance=±5% resistance=1k package=THT]
  IC1 = Voltage Regulator [package=to-220-alt]
  C1 = [richard] Capacitor 100nF [package="7.5mm [THT, pp]"]
  C2 = [richard] Capacitor 100nF [package="7.5mm [THT, pp]"]
  VCC1 = Battery block 9V
  S1 = Round Pushbutton
  LED1 = RGB LED (com. cathode, rgb) [package="5 mm [THT]"]

nets:
  N1: R1.Pin_0, Composant1.D3
  N2: R1.Pin_1, Q1.B
  N3: Q1.E, LED1.blue_anode
  N4: Q1.C, Q2.C, Q3.C, U1.E, IC1.OUT, C2.-
  N5: Q2.E, LED1.green_anode
  N6: Q2.B, R2.Pin_1
  N7: Q3.E, LED1.red_anode
  N8: Q3.B, R3.Pin_1
  GND: Composant1.GND, U1.A, IC1.GND, C1.+, C2.+, VCC1.-, S1.leg0, LED1.common_cathode
  N9: Composant1.D2, S1.leg1
  N10: Composant1.D5, R2.Pin_0
  N11: Composant1.D6, R3.Pin_0
  N12: Composant1.VIN, IC1.IN, C1.-, VCC1.+
  N13: Composant1.A0, U1.S

custom parts:
  [richard] Capacitor 100nF: Polypropylene/Film and Foil capacitor.
